// Logisim project Trabalhofinal.sistemas.FINAL.circ as structural Verilog: 2 circuits, main circuit main
module main (
  output Q2,
  output Q1,
  output Q0,
  output d0,
  output d1,
  output d2
);

  wire _1_out, _2_out, _3_out, _4_out, _5_out, _6_out, A7, and_1_out, and_2_out, and_4_out, and_5_out,
       and_6_out, and_7_out, and_8_out, and_9_out, and_10_out, and_11_out, and_12_out, and_13_out, B7, bake,
       C7, Carregue_para_assar_a_Pizza_out, clock_1_out, COIN__1, COIN__2, comparator_1_eq, comparator_2_lt,
       comparator_3_eq, comparator_4_eq, comparator_5_eq, comparator_6_eq, comparator_6_lt, comparator_7_eq,
       comparator_8_eq, comparator_9_eq, comparator_10_eq, counter_3_q, D7, E7, F7, FIM__RESET, G7,
       LedMoneyOK, not_1_out, not_2_out, not_3_out, not_4_out, not_5_out, not_6_out, not_7_out, not_8_out,
       not_9_out, not_10_out, not_11_out, not_12_out, not_13_out, not_14_out, not_15_out, not_16_out,
       not_17_out, not_18_out, not_19_out, not_20_out, not_21_out, or_2_out, or_3_out, or_5_out, or_9_out,
       pizzapronta, Reset_Coin, Reset_Moedas_out;
  wire [3:0] counter_1_q, counter_2_q;

  or or_1 (Reset_Coin, FIM__RESET, Reset_Moedas_out);
  Counter #(.width(4), .max('hf)) counter_1 (
    .Q(counter_1_q), .clk(COIN__2), .clr(Reset_Coin));  // open: load, D, count, carry
  Counter #(.width(4), .max('hf)) counter_2 (
    .Q(counter_2_q), .clk(COIN__1), .clr(Reset_Coin));  // open: load, D, count, carry
  _7_Segment_Display u_7_segment_display_1 (.g(G7), .f(F7), .a(A7), .b(B7), .e(E7), .d(D7), .c(C7));  // open: dp
  Button button_1 (.out(COIN__1));
  Button button_2 (.out(COIN__2));
  Button Reset_Moedas (.out(Reset_Moedas_out));
  Comparator #(.width(4)) comparator_1 (.a(4'b0010), .b(counter_2_q), .eq(comparator_1_eq));  // open: gt, lt
  Comparator #(.width(4)) comparator_2 (.a(4'b0011), .b(counter_2_q), .lt(comparator_2_lt));  // open: gt, eq
  Comparator #(.width(4)) comparator_3 (.a(4'b0011), .b(counter_2_q), .eq(comparator_3_eq));  // open: gt, lt
  Comparator #(.width(4)) comparator_4 (.a(4'b0001), .b(counter_2_q), .eq(comparator_4_eq));  // open: gt, lt
  Comparator #(.width(4)) comparator_5 (.a(4'b0001), .b(counter_1_q), .eq(comparator_5_eq));  // open: gt, lt
  Comparator #(.width(4)) comparator_6 (
    .a(4'b0010), .b(counter_1_q), .eq(comparator_6_eq), .lt(comparator_6_lt));  // open: gt
  LED Dinheiro_ok (.in(LedMoneyOK));
  and and_1 (and_1_out, comparator_4_eq, comparator_5_eq);
  or or_2 (or_2_out, comparator_6_eq, comparator_6_lt);
  or or_3 (or_3_out, comparator_1_eq, comparator_5_eq);
  Button Carregue_para_assar_a_Pizza (.out(Carregue_para_assar_a_Pizza_out));
  and and_2 (and_2_out, or_3_out, comparator_4_eq);
  display7seg display7seg_1 (
    .X(or_5_out), .Y(or_3_out), .Z(comparator_4_eq), .a(A7), .b(B7), .c(C7), .d(D7), .e(E7), .f(F7), .g(G7));
  LED \Pizza_está_servida  (.in(pizzapronta));
  or or_4 (LedMoneyOK, or_5_out, and_2_out);
  or or_5 (or_5_out, comparator_2_lt, comparator_3_eq, and_1_out, or_2_out);
  and and_3 (bake, LedMoneyOK, Carregue_para_assar_a_Pizza_out);
  Counter #(.width(1), .max('h1), .ongoal("stay")) counter_3 (
    .Q(counter_3_q), .clk(bake), .clr(FIM__RESET));  // open: load, D, count, carry
  not not_1 (not_1_out, counter_3_q);
  not not_2 (not_2_out, Q1);
  not not_3 (not_3_out, counter_3_q);
  not not_4 (not_4_out, Q2);
  not not_5 (not_5_out, Q0);
  not not_6 (not_6_out, Q1);
  not not_7 (not_7_out, counter_3_q);
  not not_8 (not_8_out, counter_3_q);
  not not_9 (not_9_out, Q2);
  not not_10 (not_10_out, Q0);
  not not_11 (not_11_out, Q1);
  not not_12 (not_12_out, Q0);
  and and_4 (and_4_out, not_1_out, Q2);
  or or_6 (d0, and_4_out, and_5_out, and_6_out);
  and and_5 (and_5_out, Q2, not_2_out);
  and and_6 (and_6_out, counter_3_q, Q1, Q0);
  and and_7 (and_7_out, not_3_out, Q1);
  and and_8 (and_8_out, not_4_out, Q1, not_5_out);
  or or_7 (d1, and_7_out, and_8_out, and_9_out);
  and and_9 (and_9_out, counter_3_q, not_6_out, Q0);
  and and_10 (and_10_out, not_7_out, Q1, Q0);
  and and_11 (and_11_out, not_8_out, Q2, Q0);
  and and_12 (and_12_out, counter_3_q, not_9_out, not_10_out);
  and and_13 (and_13_out, counter_3_q, not_11_out, not_12_out);
  or or_8 (d2, and_10_out, and_11_out, and_12_out, and_13_out);
  Clock clock_1 (.out(clock_1_out));
  D_Flip_Flop d_ff_1 (.clk(clock_1_out), .D(d2), .Q(Q0), .reset(FIM__RESET));  // open: Qn, preset, en
  D_Flip_Flop d_ff_2 (.clk(clock_1_out), .D(d1), .Q(Q1), .reset(FIM__RESET));  // open: Qn, preset, en
  D_Flip_Flop d_ff_3 (.clk(clock_1_out), .D(d0), .Q(Q2), .reset(FIM__RESET));  // open: Qn, preset, en
  not not_13 (not_13_out, Q1);
  not not_14 (not_14_out, Q2);
  not not_15 (not_15_out, Q0);
  not not_16 (not_16_out, Q2);
  not not_17 (not_17_out, Q2);
  not not_18 (not_18_out, Q1);
  not not_19 (not_19_out, Q0);
  not not_20 (not_20_out, Q1);
  not not_21 (not_21_out, Q0);
  and _1 (_1_out, Q0, not_13_out, not_14_out);
  and _2 (_2_out, Q1, not_15_out, not_16_out);
  and _3 (_3_out, Q0, Q1, not_17_out);
  and _4 (_4_out, Q2, not_18_out, not_19_out);
  and _5 (_5_out, Q0, Q2, not_20_out);
  and _6 (_6_out, Q1, Q2, not_21_out);
  Comparator #(.width(1)) comparator_7 (.a(1'b1), .b(_1_out), .eq(comparator_7_eq));  // open: gt, lt
  Comparator #(.width(1)) comparator_8 (.a(1'b1), .b(_2_out), .eq(comparator_8_eq));  // open: gt, lt
  Comparator #(.width(1)) comparator_9 (.a(1'b1), .b(_3_out), .eq(comparator_9_eq));  // open: gt, lt
  Comparator #(.width(1)) comparator_10 (.a(1'b1), .b(_4_out), .eq(comparator_10_eq));  // open: gt, lt
  Comparator #(.width(1)) comparator_11 (.a(1'b1), .b(_5_out), .eq(pizzapronta));  // open: gt, lt
  Comparator #(.width(1)) comparator_12 (.a(1'b1), .b(_6_out), .eq(FIM__RESET));  // open: gt, lt
  LED Pizza_retirada_do_congelador_e_colocada_no_forno (.in(comparator_7_eq));
  LED Pizza_no_Forno (.in(or_9_out));
  or or_9 (or_9_out, comparator_8_eq, comparator_9_eq);
  LED \Pizza_já_está_pronta_e_será_servida  (.in(comparator_10_eq));

  // Notes on the sheet:
  //   Moeda 1E
  //   Moeda 2E
  //   2 euros 
  //   4 ou + euros
  //   Moedeiro
  //   2 euros
  //   >3 euros
  //   =3 euros
  //   1euro
  //   Ecrã
  //   Preparo da Pizza
endmodule

module display7seg (
  input  X,
  input  Y,
  input  Z,
  output a,
  output b,
  output c,
  output d,
  output e,
  output f,
  output g
);

  wire not_1_out, not_2_out, not_3_out, not_4_out, not_5_out, not_6_out, not_7_out, not_8_out;

  not not_1 (not_1_out, Z);
  not not_2 (not_2_out, Y);
  not not_3 (not_3_out, Z);
  not not_4 (not_4_out, X);
  not not_5 (not_5_out, Z);
  not not_6 (not_6_out, X);
  not not_7 (not_7_out, Y);
  not not_8 (not_8_out, Z);
  or or_1 (g, Y, X);
  or or_2 (a, not_1_out, Y, X);
  or or_3 (c, not_2_out, Z, X);
  or or_4 (d, not_3_out, Y, X);
  and and_1 (e, not_4_out, not_5_out);
  and and_2 (f, not_6_out, not_7_out, not_8_out);

  assign b = 1'b1;
endmodule
