// Logisim project Trabalhofinal.sistemas.display7seg.circ as structural Verilog
module main (
  input  in_1,
  input  in_2,
  input  in_3,
  input  in_4,
  input  in_5,
  input  in_6,
  input  in_7,
  input  in_8,
  input  in_9,
  input  M,
  input  in_11,
  output Q3,
  output Q2,
  output Q1,
  output Q0
);

  wire _1_out, _2_out, _3_out, _4_out, _5_out, _6_out, A7, and_1_out, and_2_out, and_3_out, and_5_out,
       and_6_out, and_7_out, and_8_out, and_9_out, and_10_out, and_11_out, and_12_out, and_13_out,
       and_14_out, and_15_out, and_16_out, and_17_out, and_18_out, and_19_out, and_20_out, and_21_out,
       and_22_out, and_23_out, and_24_out, and_25_out, and_26_out, and_27_out, and_28_out, and_29_out,
       and_30_out, and_31_out, and_32_out, and_33_out, B7, bake, button_3_out, C7, clock_1_out, clock_2_out,
       clock_3_out, clock_4_out, COIN__1, COIN__2, comparator_1_eq, comparator_2_eq, comparator_3_eq,
       comparator_4_eq, comparator_5_eq, comparator_7_eq, comparator_8_lt, comparator_9_eq, comparator_10_eq,
       comparator_11_eq, comparator_12_eq, comparator_12_lt, counter_1_q, D0_q, D1_q, D7, E7, F7, FIM__RESET,
       G7, LedMoneyOK, not_1_out, not_2_out, not_3_out, not_4_out, not_5_out, not_6_out, not_7_out,
       not_8_out, not_9_out, not_10_out, not_11_out, not_12_out, not_13_out, not_14_out, not_15_out,
       not_16_out, not_17_out, not_18_out, not_19_out, not_20_out, not_21_out, not_22_out, not_23_out,
       not_24_out, not_25_out, not_26_out, not_27_out, not_28_out, not_29_out, not_30_out, not_31_out,
       not_32_out, not_33_out, not_34_out, not_35_out, not_36_out, not_37_out, not_38_out, not_39_out,
       not_40_out, not_41_out, not_42_out, or_1_out, or_2_out, or_3_out, or_5_out, or_6_out, or_7_out,
       or_8_out, or_9_out, or_10_out, or_11_out, or_12_out, or_13_out, or_14_out, or_15_out, or_16_out,
       Reset_Coin, START, xor_1_out, xor_2_out, xor_3_out, xor_4_out;
  wire [3:0] counter_2_q, counter_3_q;

  Button button_1 (.out(COIN__1));
  Button button_2 (.out(COIN__2));
  Counter #(.width(1), .max('h1), .ongoal("stay")) counter_1 (
    .Q(counter_1_q), .clk(bake));  // open: load, D, count, carry, clr
  _7_Segment_Display u_7_segment_display_1 (.g(G7), .f(F7), .a(A7), .b(B7), .e(E7), .d(D7), .c(C7));  // open: dp
  Button reset (.out(Reset_Coin));
  and and_1 (and_1_out, counter_1_q, Q0);
  and and_2 (and_2_out, and_1_out, Q1);
  and and_3 (and_3_out, and_2_out, Q2);
  xor xor_1 (xor_1_out, Q0, counter_1_q);
  xor xor_2 (xor_2_out, Q1, and_1_out);
  xor xor_3 (xor_3_out, Q2, and_2_out);
  xor xor_4 (xor_4_out, Q3, and_3_out);
  LED led_1 (.in(LedMoneyOK));
  Button Carregue_para_assar_a_Pizza (.out(START));
  D_Flip_Flop d_ff_1 (.clk(clock_1_out), .D(xor_1_out), .Q(Q0));  // open: Qn, preset, en, reset
  D_Flip_Flop d_ff_2 (.clk(clock_1_out), .D(xor_2_out), .Q(Q1));  // open: Qn, preset, en, reset
  D_Flip_Flop d_ff_3 (.clk(clock_1_out), .D(xor_3_out), .Q(Q2));  // open: Qn, preset, en, reset
  D_Flip_Flop d_ff_4 (.clk(clock_1_out), .D(xor_4_out), .Q(Q3));  // open: Qn, preset, en, reset
  and and_4 (bake, LedMoneyOK, START);
  Clock clock_1 (.out(clock_1_out));
  not not_1 (not_1_out, Q1);
  not not_2 (not_2_out, Q2);
  not not_3 (not_3_out, Q3);
  not not_4 (not_4_out, Q0);
  not not_5 (not_5_out, Q2);
  not not_6 (not_6_out, Q3);
  not not_7 (not_7_out, Q2);
  not not_8 (not_8_out, Q3);
  not not_9 (not_9_out, Q1);
  not not_10 (not_10_out, Q0);
  not not_11 (not_11_out, Q3);
  not not_12 (not_12_out, Q1);
  not not_13 (not_13_out, Q3);
  not not_14 (not_14_out, Q0);
  and _1 (_1_out, Q0, not_1_out, not_2_out, not_3_out);
  and _2 (_2_out, Q1, not_4_out, not_5_out, not_6_out);
  and _3 (_3_out, Q0, Q1, not_7_out, not_8_out);
  and _4 (_4_out, Q2, not_9_out, not_10_out, not_11_out);
  and _5 (_5_out, Q0, Q2, not_12_out, not_13_out);
  and _6 (_6_out, Q1, Q2, not_14_out);
  Counter #(.width(4), .max('hf)) counter_2 (
    .Q(counter_2_q), .clk(COIN__2), .clr(Reset_Coin));  // open: load, D, count, carry
  Counter #(.width(4), .max('hf)) counter_3 (
    .Q(counter_3_q), .clk(COIN__1), .clr(Reset_Coin));  // open: load, D, count, carry
  Comparator #(.width(1)) comparator_1 (.a(1'b1), .b(_1_out), .eq(comparator_1_eq));  // open: gt, lt
  Comparator #(.width(1)) comparator_2 (.a(1'b1), .b(_2_out), .eq(comparator_2_eq));  // open: gt, lt
  Comparator #(.width(1)) comparator_3 (.a(1'b1), .b(_3_out), .eq(comparator_3_eq));  // open: gt, lt
  Comparator #(.width(1)) comparator_4 (.a(1'b1), .b(_4_out), .eq(comparator_4_eq));  // open: gt, lt
  Comparator #(.width(1)) comparator_5 (.a(1'b1), .b(_5_out), .eq(comparator_5_eq));  // open: gt, lt
  Comparator #(.width(1)) comparator_6 (.a(1'b1), .b(_6_out), .eq(FIM__RESET));  // open: gt, lt
  LED Pizza_retirada_do_congelador_e_colocada_no_forno (.in(comparator_1_eq));
  Comparator #(.width(4)) comparator_7 (.a(4'b0010), .b(counter_3_q), .eq(comparator_7_eq));  // open: gt, lt
  Comparator #(.width(4)) comparator_8 (.a(4'b0011), .b(counter_3_q), .lt(comparator_8_lt));  // open: gt, eq
  Comparator #(.width(4)) comparator_9 (.a(4'b0011), .b(counter_3_q), .eq(comparator_9_eq));  // open: gt, lt
  Comparator #(.width(4)) comparator_10 (.a(4'b0001), .b(counter_3_q), .eq(comparator_10_eq));  // open: gt, lt
  Comparator #(.width(4)) comparator_11 (.a(4'b0001), .b(counter_2_q), .eq(comparator_11_eq));  // open: gt, lt
  Comparator #(.width(4)) comparator_12 (
    .a(4'b0010), .b(counter_2_q), .eq(comparator_12_eq), .lt(comparator_12_lt));  // open: gt
  LED Pizza_no_Forno (.in(or_1_out));
  or or_1 (or_1_out, comparator_2_eq, comparator_3_eq);
  LED \Pizza_já_está_pronta_e_será_servida  (.in(comparator_4_eq));
  LED \Pizza_está_servida  (.in(comparator_5_eq));
  and and_5 (and_5_out, comparator_10_eq, comparator_11_eq);
  or or_2 (or_2_out, comparator_12_eq, comparator_12_lt);
  or or_3 (or_3_out, comparator_7_eq, comparator_11_eq);
  and and_6 (and_6_out, or_3_out, comparator_10_eq);
  display7seg display7seg_1 (
    .X(or_5_out), .Y(or_3_out), .Z(comparator_10_eq), .a(A7), .b(B7), .c(C7), .d(D7), .e(E7), .f(F7), .g(G7));
  or or_4 (LedMoneyOK, or_5_out, and_6_out);
  or or_5 (or_5_out, comparator_8_lt, comparator_9_eq, and_5_out, or_2_out);
  Button button_3 (.out(button_3_out));
  Clock clock_2 (.out(clock_2_out));
  D_Flip_Flop d_ff_5 (.clk(clock_2_out), .D(or_6_out), .Q(in_1));  // open: Qn, preset, en, reset
  not not_15 (not_15_out, in_2);
  not not_16 (not_16_out, in_3);
  not not_17 (not_17_out, in_1);
  not not_18 (not_18_out, in_1);
  not not_19 (not_19_out, in_2);
  D_Flip_Flop d_ff_6 (.clk(clock_2_out), .D(or_7_out), .Q(in_2));  // open: Qn, preset, en, reset
  not not_20 (not_20_out, in_3);
  and and_7 (and_7_out, not_15_out, in_1);
  and and_8 (and_8_out, in_2, in_3);
  and and_9 (and_9_out, not_16_out, in_2);
  and and_10 (and_10_out, not_17_out, in_3);
  D_Flip_Flop d_ff_7 (.clk(clock_2_out), .D(or_8_out), .Q(in_3));  // open: Qn, preset, en, reset
  or or_6 (or_6_out, and_7_out, and_8_out);
  and and_11 (and_11_out, not_18_out, not_19_out, button_3_out);
  or or_7 (or_7_out, and_9_out, and_10_out);
  or or_8 (or_8_out, and_11_out, not_20_out);
  not not_21 (not_21_out, D0_q);
  not not_22 (not_22_out, D1_q);
  not not_23 (not_23_out, D0_q);
  buf and_12 (and_12_out, D0_q);  // AND_Gate
  and and_13 (and_13_out, not_21_out, D1_q);
  and and_14 (and_14_out, not_22_out, D0_q);
  and and_15 (and_15_out, D1_q, not_23_out);
  or or_9 (or_9_out, and_12_out, and_13_out);
  or or_10 (or_10_out, and_14_out, and_15_out);
  Clock clock_3 (.out(clock_3_out));
  D_Flip_Flop D0 (.D(or_9_out), .Q(D0_q));  // open: clk, Qn, preset, en, reset
  D_Flip_Flop d_ff_8 (.clk(clock_3_out), .D(or_11_out), .Q(in_7));  // open: Qn, preset, en, reset
  not not_24 (not_24_out, in_8);
  D_Flip_Flop D1 (.D(or_10_out), .Q(D1_q));  // open: clk, Qn, preset, en, reset
  D_Flip_Flop d_ff_9 (.clk(clock_3_out), .D(or_12_out), .Q(in_8));  // open: Qn, preset, en, reset
  and and_16 (and_16_out, in_8, in_9);
  and and_17 (and_17_out, in_7, not_24_out);
  not not_25 (not_25_out, in_9);
  not not_26 (not_26_out, in_9);
  not not_27 (not_27_out, in_7);
  not not_28 (not_28_out, in_8);
  and and_18 (and_18_out, D0_q, D1_q);
  D_Flip_Flop d_ff_10 (.clk(clock_3_out), .D(or_13_out), .Q(in_9));  // open: Qn, preset, en, reset
  or or_11 (or_11_out, and_16_out, and_17_out);
  and and_19 (and_19_out, in_9, not_27_out);
  and and_20 (and_20_out, not_25_out, in_8);
  and and_21 (and_21_out, in_11, not_26_out);
  and and_22 (and_22_out, not_28_out, in_9);
  or or_12 (or_12_out, and_19_out, and_20_out);
  or or_13 (or_13_out, and_21_out, and_22_out);
  Clock clock_4 (.out(clock_4_out));
  D_Flip_Flop d_ff_11 (.clk(clock_4_out), .D(or_14_out), .Q(in_4));  // open: Qn, preset, en, reset
  not not_29 (not_29_out, in_5);
  not not_30 (not_30_out, M);
  not not_31 (not_31_out, in_6);
  not not_32 (not_32_out, M);
  not not_33 (not_33_out, in_5);
  not not_34 (not_34_out, in_5);
  not not_35 (not_35_out, in_4);
  not not_36 (not_36_out, in_6);
  not not_37 (not_37_out, in_5);
  not not_38 (not_38_out, in_6);
  not not_39 (not_39_out, in_5);
  D_Flip_Flop d_ff_12 (.clk(clock_4_out), .D(or_16_out), .Q(in_5));  // open: Qn, preset, en, reset
  not not_40 (not_40_out, in_6);
  not not_41 (not_41_out, M);
  not not_42 (not_42_out, in_4);
  and and_23 (and_23_out, not_29_out, in_6);
  and and_24 (and_24_out, not_30_out, in_4, not_31_out);
  and and_25 (and_25_out, M, in_5, in_6);
  and and_26 (and_26_out, not_32_out, in_5);
  and and_27 (and_27_out, M, in_4, not_33_out);
  and and_28 (and_28_out, M, not_34_out, in_6);
  and and_29 (and_29_out, M, not_35_out, in_5, not_36_out);
  and and_30 (and_30_out, M, not_40_out);
  and and_31 (and_31_out, M, not_37_out, not_38_out);
  and and_32 (and_32_out, M, not_39_out, in_6);
  and and_33 (and_33_out, not_41_out, not_42_out, in_5);
  D_Flip_Flop d_ff_13 (.clk(clock_4_out), .D(or_15_out), .Q(in_6));  // open: Qn, preset, en, reset
  or or_14 (or_14_out, and_23_out, and_24_out, and_25_out);
  or or_15 (or_15_out, and_30_out, and_31_out, and_32_out, and_33_out);
  or or_16 (or_16_out, and_26_out, and_27_out, and_28_out, and_29_out);

  // Notes on the sheet:
  //   1 euro
  //   2 euros
  //   2 euros 
  //   4 ou + euros
  //   2 euros
  //   >3 euros
  //   =3 euros
  //   1euro
endmodule

module display7seg (
  input  X,
  input  Y,
  input  Z,
  output a,
  output b,
  output c,
  output d,
  output e,
  output f,
  output g
);

  wire not_1_out, not_2_out, not_3_out, not_4_out, not_5_out, not_6_out, not_7_out, not_8_out;

  not not_1 (not_1_out, Z);
  not not_2 (not_2_out, Y);
  not not_3 (not_3_out, Z);
  not not_4 (not_4_out, X);
  not not_5 (not_5_out, Z);
  not not_6 (not_6_out, X);
  not not_7 (not_7_out, Y);
  not not_8 (not_8_out, Z);
  or or_1 (g, Y, X);
  or or_2 (a, not_1_out, Y, X);
  or or_3 (c, not_2_out, Z, X);
  or or_4 (d, not_3_out, Y, X);
  and and_1 (e, not_4_out, not_5_out);
  and and_2 (f, not_6_out, not_7_out, not_8_out);

  assign b = 1'b1;
endmodule
