// Logisim project Trabalhofinal.sistemas.display7seglinhas auis.circ as structural Verilog: 2 circuits, main circuit main
module main (
  input  [1:0] in_1,
  input  [1:0] in_2,
  input  [1:0] in_3,
  input  [1:0] in_4,
  input  [1:0] in_5
);

  wire A7, and_1_out, B7, button_1_out, button_2_out, C7, comparator_1_eq, comparator_2_eq, comparator_3_eq,
       comparator_5_eq, comparator_5_gt, D7, E7, F7, G7, LedMoneyOK, or_1_out, or_2_out, reset_out;
  wire [1:0] counter_1_q, counter_2_q;

  _7_Segment_Display u_7_segment_display_1 (.g(F7), .f(G7), .a(A7), .b(B7), .e(E7), .d(D7), .c(C7));  // open: dp
  LED led_1 (.in(LedMoneyOK));
  Button button_1 (.out(button_1_out));
  Button reset (.out(reset_out));
  Button button_2 (.out(button_2_out));
  Counter #(.width(2), .max('h3)) counter_1 (
    .Q(counter_1_q), .clk(button_1_out), .clr(reset_out));  // open: load, D, count, carry
  Counter #(.width(2), .max('h3)) counter_2 (
    .Q(counter_2_q), .clk(button_2_out), .clr(reset_out));  // open: load, D, count, carry
  Comparator #(.width(2)) comparator_1 (.a(in_1), .b(counter_1_q), .eq(comparator_1_eq));  // open: gt, lt
  Comparator #(.width(2)) comparator_2 (.a(in_2), .b(counter_1_q), .eq(comparator_2_eq));  // open: gt, lt
  Comparator #(.width(2)) comparator_3 (.a(in_3), .b(counter_1_q), .eq(comparator_3_eq));  // open: gt, lt
  Comparator #(.width(2)) comparator_4 (.a(in_4), .b(counter_2_q), .eq(comparator_1_eq));  // open: gt, lt
  Comparator #(.width(2)) comparator_5 (
    .a(in_5), .b(counter_2_q), .gt(comparator_5_gt), .eq(comparator_5_eq));  // open: lt
  and and_1 (and_1_out, comparator_3_eq, comparator_1_eq);
  or or_1 (or_1_out, comparator_5_gt, comparator_5_eq);
  display7seg display7seg_1 (
    .X(or_2_out), .Y(comparator_1_eq), .Z(comparator_3_eq), .a(A7), .b(B7), .c(C7), .d(D7), .e(E7), .f(F7),
    .g(G7));
  or or_2 (or_2_out, comparator_2_eq, and_1_out, or_1_out);

  // Notes on the sheet:
  //   1 euro
  //   2 euros
  //   2 euros
  //   3 euros
  //   1euro
  //   2 euros 
  //   4 ou + euros
endmodule

module display7seg (
  input  X,
  input  Y,
  input  Z,
  output a,
  output b,
  output c,
  output d,
  output e,
  output f,
  output g
);

  wire and_1_out, LedMoneyOK, not_1_out, not_2_out, not_3_out, not_4_out, not_5_out, not_6_out, not_7_out,
       not_8_out;

  and and_1 (and_1_out, Y, Z);
  not not_1 (not_1_out, Z);
  or or_1 (a, not_1_out, Y, X);
  not not_2 (not_2_out, Y);
  or or_2 (c, not_2_out, Z, X);
  not not_3 (not_3_out, Z);
  or or_3 (d, not_3_out, Y, X);
  not not_4 (not_4_out, X);
  and and_2 (e, not_4_out, not_5_out);
  not not_5 (not_5_out, Z);
  not not_6 (not_6_out, X);
  and and_3 (f, not_6_out, not_7_out, not_8_out);
  not not_7 (not_7_out, Y);
  not not_8 (not_8_out, Z);
  or or_4 (g, Y, X);
  or or_5 (LedMoneyOK, X, and_1_out);

  assign b = 1'b1;
endmodule
