// Logisim project Trabalhofinal.sistemas.parcial.circ as structural Verilog: 3 circuits, main circuit main
module main (
  input  [3:0] in_1,
  input  [3:0] _3_euros,
  input  [3:0] _3_euros_2,
  input  [3:0] in_4,
  input  [3:0] _2_euros,
  input  [3:0] _4_ou___euros
);

  wire A7, and_1_out, and_2_out, B7, C7, COIN__1, COIN__2, comparator_1_eq, comparator_2_lt, comparator_3_eq,
       comparator_4_eq, comparator_5_eq, comparator_6_eq, comparator_6_lt, D7, E7, F7, G7, LedMoneyOK,
       or_1_out, or_2_out, or_4_out, Reset_Coin, START;
  wire [3:0] counter_1_q, counter_2_q;

  Button button_1 (.out(COIN__1));
  Button button_2 (.out(COIN__2));
  _7_Segment_Display u_7_segment_display_1 (.g(G7), .f(F7), .a(A7), .b(B7), .e(E7), .d(D7), .c(C7));  // open: dp
  Button reset (.out(Reset_Coin));
  LED led_1 (.in(LedMoneyOK));
  Button Carregue_para_assar_a_Pizza (.out(START));
  Counter #(.width(4), .max('hf)) counter_1 (
    .Q(counter_1_q), .clk(COIN__2), .clr(Reset_Coin));  // open: load, D, count, carry
  Counter #(.width(4), .max('hf)) counter_2 (
    .Q(counter_2_q), .clk(COIN__1), .clr(Reset_Coin));  // open: load, D, count, carry
  Comparator #(.width(4)) comparator_1 (.a(in_1), .b(counter_2_q), .eq(comparator_1_eq));  // open: gt, lt
  Comparator #(.width(4)) comparator_2 (.a(_3_euros), .b(counter_2_q), .lt(comparator_2_lt));  // open: gt, eq
  Comparator #(.width(4)) comparator_3 (.a(_3_euros_2), .b(counter_2_q), .eq(comparator_3_eq));  // open: gt, lt
  Comparator #(.width(4)) comparator_4 (.a(in_4), .b(counter_2_q), .eq(comparator_4_eq));  // open: gt, lt
  Comparator #(.width(4)) comparator_5 (.a(_2_euros), .b(counter_1_q), .eq(comparator_5_eq));  // open: gt, lt
  Comparator #(.width(4)) comparator_6 (
    .a(_4_ou___euros), .b(counter_1_q), .eq(comparator_6_eq), .lt(comparator_6_lt));  // open: gt
  and and_1 (and_1_out, comparator_4_eq, comparator_5_eq);
  or or_1 (or_1_out, comparator_6_eq, comparator_6_lt);
  or or_2 (or_2_out, comparator_1_eq, comparator_5_eq);
  and and_2 (and_2_out, or_2_out, comparator_4_eq);
  display7seg display7seg_1 (
    .X(or_4_out), .Y(or_2_out), .Z(comparator_4_eq), .a(A7), .b(B7), .c(C7), .d(D7), .e(E7), .f(F7), .g(G7));
  or or_3 (LedMoneyOK, or_4_out, and_2_out);
  or or_4 (or_4_out, comparator_2_lt, comparator_3_eq, and_1_out, or_1_out);

  // Notes on the sheet:
  //   1 euro
  //   2 euros
  //   2 euros
  //   1euro
endmodule

module display7seg (
  input  X,
  input  Y,
  input  Z,
  output a,
  output b,
  output c,
  output d,
  output e,
  output f,
  output g
);

  wire not_1_out, not_2_out, not_3_out, not_4_out, not_5_out, not_6_out, not_7_out, not_8_out;

  not not_1 (not_1_out, Z);
  not not_2 (not_2_out, Y);
  not not_3 (not_3_out, Z);
  not not_4 (not_4_out, X);
  not not_5 (not_5_out, Z);
  not not_6 (not_6_out, X);
  not not_7 (not_7_out, Y);
  not not_8 (not_8_out, Z);
  or or_1 (g, Y, X);
  or or_2 (a, not_1_out, Y, X);
  or or_3 (c, not_2_out, Z, X);
  or or_4 (d, not_3_out, Y, X);
  and and_1 (e, not_4_out, not_5_out);
  and and_2 (f, not_6_out, not_7_out, not_8_out);

  assign b = 1'b1;
endmodule

module forno (
  input  OutFreezer,
  input  Bake,
  input  x1,
  input  in_4,
  input  x0,
  input  Start,
  output D1,
  output D0
);

  wire and_1_out, and_2_out, and_3_out, and_4_out, and_5_out, and_6_out, clock_1_out, clock_2_out, d_ff_1_q,
       d_ff_2_q, not_1_out, not_2_out, not_3_out, not_4_out;

  not not_1 (not_1_out, OutFreezer);
  not not_2 (not_2_out, x1);
  not not_3 (not_3_out, x0);
  not not_4 (not_4_out, x0);
  and and_1 (and_1_out, x0, OutFreezer);
  and and_2 (and_2_out, x1, x0, Bake);
  and and_3 (and_3_out, not_2_out, not_3_out, Start);
  and and_4 (and_4_out, x0, not_4_out, not_1_out);
  and and_5 (and_5_out, x0, x0, Bake);
  or or_1 (D1, and_1_out, and_2_out);
  or or_2 (D0, and_3_out, and_4_out, and_5_out);
  Clock clock_1 (.out(clock_1_out));
  Clock clock_2 (.out(clock_2_out));
  D_Flip_Flop d_ff_1 (.clk(clock_1_out), .D(D1), .Q(d_ff_1_q));  // open: Qn, preset, en, reset
  and and_6 (and_6_out, d_ff_1_q, d_ff_2_q);
  D_Flip_Flop d_ff_2 (.clk(clock_2_out), .D(D0), .Q(d_ff_2_q));  // open: Qn, preset, en, reset
endmodule
